# Fritzing sketch Bapsim_All_Sensors (saved by Fritzing 0.9.5d)

parts:
  DK_/_USB_at_top = nRF54LM20-DK PCA10184 0.7.0 (selected pins)
  MB-102_/_top-number_coordinate_reference = MB-102 reference grid 0-62 / top-number convention
  LDR_1_/_잠금_표시 = GL5528
  R1_10k_/_divider = 10k ohm 1% resistor
  R2_10k_/_ADC_series = 10k ohm 1% resistor
  LDR_2_/_보온_표시 = GL5528
  R3_10k_/_divider = 10k ohm 1% resistor
  R4_10k_/_ADC_series = 10k ohm 1% resistor
  LDR_3_/_백미_표시 = GL5528
  R5_10k_/_divider = 10k ohm 1% resistor
  R6_10k_/_ADC_series = 10k ohm 1% resistor
  LDR_4_/_시간_첫_표시 = GL5528
  R7_10k_/_divider = 10k ohm 1% resistor
  R8_10k_/_ADC_series = 10k ohm 1% resistor
  NTC_/_외부_표면 = NTC probe
  R9_10k_/_NTC_pull-up = 10k ohm 1% resistor
  R10_10k_/_ADC_series = 10k ohm 1% resistor
  개폐_/_뚜껑·본체 = 5C-39 NO
  R11_10k_/_contact_pull-up = 10k ohm 1% resistor

nets:
  N1: DK_/_USB_at_top.GND, MB-102_/_top-number_coordinate_reference.A53, MB-102_/_top-number_coordinate_reference.B17, MB-102_/_top-number_coordinate_reference.B32, MB-102_/_top-number_coordinate_reference.B53, MB-102_/_top-number_coordinate_reference.BLN1, MB-102_/_top-number_coordinate_reference.BLN12, MB-102_/_top-number_coordinate_reference.BLN13, MB-102_/_top-number_coordinate_reference.BLN24, MB-102_/_top-number_coordinate_reference.BRN0, MB-102_/_top-number_coordinate_reference.BRN20, MB-102_/_top-number_coordinate_reference.C17, MB-102_/_top-number_coordinate_reference.C32, MB-102_/_top-number_coordinate_reference.H17, MB-102_/_top-number_coordinate_reference.H32, MB-102_/_top-number_coordinate_reference.I17, MB-102_/_top-number_coordinate_reference.I32, MB-102_/_top-number_coordinate_reference.I53, MB-102_/_top-number_coordinate_reference.J53, MB-102_/_top-number_coordinate_reference.TLN0, MB-102_/_top-number_coordinate_reference.TLN1, MB-102_/_top-number_coordinate_reference.TLN10, MB-102_/_top-number_coordinate_reference.TLN11, MB-102_/_top-number_coordinate_reference.TLN24, MB-102_/_top-number_coordinate_reference.TRN0, MB-102_/_top-number_coordinate_reference.TRN20, R1_10k_/_divider.connector1, R3_10k_/_divider.connector1, R5_10k_/_divider.connector1, R7_10k_/_divider.connector1, NTC_/_외부_표면.connector1, 개폐_/_뚜껑·본체.connector1
  N2: DK_/_USB_at_top.P1_03, MB-102_/_top-number_coordinate_reference.C22, MB-102_/_top-number_coordinate_reference.E22, R2_10k_/_ADC_series.connector1
  N3: DK_/_USB_at_top.P1_04, MB-102_/_top-number_coordinate_reference.C37, MB-102_/_top-number_coordinate_reference.E37, R4_10k_/_ADC_series.connector1
  N4: DK_/_USB_at_top.P1_05, MB-102_/_top-number_coordinate_reference.F22, MB-102_/_top-number_coordinate_reference.H22, R6_10k_/_ADC_series.connector1
  N5: DK_/_USB_at_top.P1_06, MB-102_/_top-number_coordinate_reference.F37, MB-102_/_top-number_coordinate_reference.H37, R8_10k_/_ADC_series.connector1
  N6: DK_/_USB_at_top.P1_10, MB-102_/_top-number_coordinate_reference.F48, MB-102_/_top-number_coordinate_reference.I48, MB-102_/_top-number_coordinate_reference.J48, 개폐_/_뚜껑·본체.connector0, R11_10k_/_contact_pull-up.connector1
  N7: DK_/_USB_at_top.P1_29, MB-102_/_top-number_coordinate_reference.C58, MB-102_/_top-number_coordinate_reference.E58, R10_10k_/_ADC_series.connector1
  N8: DK_/_USB_at_top.VDD_IO, MB-102_/_top-number_coordinate_reference.A10, MB-102_/_top-number_coordinate_reference.A25, MB-102_/_top-number_coordinate_reference.A43, MB-102_/_top-number_coordinate_reference.B10, MB-102_/_top-number_coordinate_reference.B25, MB-102_/_top-number_coordinate_reference.B43, MB-102_/_top-number_coordinate_reference.BLP1, MB-102_/_top-number_coordinate_reference.BLP7, MB-102_/_top-number_coordinate_reference.BLP8, MB-102_/_top-number_coordinate_reference.BLP24, MB-102_/_top-number_coordinate_reference.BRP0, MB-102_/_top-number_coordinate_reference.BRP12, MB-102_/_top-number_coordinate_reference.I10, MB-102_/_top-number_coordinate_reference.I25, MB-102_/_top-number_coordinate_reference.I43, MB-102_/_top-number_coordinate_reference.J10, MB-102_/_top-number_coordinate_reference.J25, MB-102_/_top-number_coordinate_reference.J43, MB-102_/_top-number_coordinate_reference.TLP0, MB-102_/_top-number_coordinate_reference.TLP1, MB-102_/_top-number_coordinate_reference.TLP5, MB-102_/_top-number_coordinate_reference.TLP6, MB-102_/_top-number_coordinate_reference.TLP24, MB-102_/_top-number_coordinate_reference.TRP0, MB-102_/_top-number_coordinate_reference.TRP12, LDR_1_/_잠금_표시.connector0, LDR_2_/_보온_표시.connector0, LDR_3_/_백미_표시.connector0, LDR_4_/_시간_첫_표시.connector0, R9_10k_/_NTC_pull-up.connector0, R11_10k_/_contact_pull-up.connector0
  N9: MB-102_/_top-number_coordinate_reference.A12, MB-102_/_top-number_coordinate_reference.B12, MB-102_/_top-number_coordinate_reference.C12, LDR_1_/_잠금_표시.connector1, R1_10k_/_divider.connector0, R2_10k_/_ADC_series.connector0
  N10: MB-102_/_top-number_coordinate_reference.A27, MB-102_/_top-number_coordinate_reference.B27, MB-102_/_top-number_coordinate_reference.C27, LDR_2_/_보온_표시.connector1, R3_10k_/_divider.connector0, R4_10k_/_ADC_series.connector0
  N11: MB-102_/_top-number_coordinate_reference.A48, MB-102_/_top-number_coordinate_reference.B48, MB-102_/_top-number_coordinate_reference.C48, NTC_/_외부_표면.connector0, R9_10k_/_NTC_pull-up.connector1, R10_10k_/_ADC_series.connector0
  N12: MB-102_/_top-number_coordinate_reference.H12, MB-102_/_top-number_coordinate_reference.I12, MB-102_/_top-number_coordinate_reference.J12, LDR_3_/_백미_표시.connector1, R5_10k_/_divider.connector0, R6_10k_/_ADC_series.connector0
  N13: MB-102_/_top-number_coordinate_reference.H27, MB-102_/_top-number_coordinate_reference.I27, MB-102_/_top-number_coordinate_reference.J27, LDR_4_/_시간_첫_표시.connector1, R7_10k_/_divider.connector0, R8_10k_/_ADC_series.connector0

custom parts:
  nRF54LM20-DK PCA10184 0.7.0 (selected pins): Breadboard wiring illustration only. Not a PCB footprint or simulator.
  MB-102 reference grid 0-62 / top-number convention: Breadboard wiring illustration only. Not a PCB footprint or simulator.
  GL5528: Breadboard wiring illustration only. Not a PCB footprint or simulator.
  10k ohm 1% resistor: Breadboard wiring illustration only. Not a PCB footprint or simulator.
  10k ohm 1% resistor: Breadboard wiring illustration only. Not a PCB footprint or simulator.
  NTC probe: Breadboard wiring illustration only. Not a PCB footprint or simulator.
  5C-39 NO: Breadboard wiring illustration only. Not a PCB footprint or simulator.
